// Logisim project lab06part2.circ as structural Verilog: 1 circuit, main circuit main
module main (
  input  [7:0] in_1,
  input  [7:0] in_2,
  input  in_3,
  output [7:0] out_4,
  output [7:0] out_5,
  output [7:0] out_6
);

  Adder adder_1 (.a(in_1), .b(in_2), .out(out_4), .cin(1'b0));  // open: cout
  Subtractor subtractor_1 (.a(in_1), .b(in_2), .out(out_6), .bin(1'b0));  // open: bout
  Multiplexer #(.width(8)) multiplexer_1 (.in0(out_4), .in1(out_6), .out(out_5), .sel(in_3));  // open: en
endmodule
