// Logisim project lab07part2.circ as structural Verilog: 2 circuits, main circuit main
module main (
  input  [7:0] in_1
);

  wire bcd_digit_1_a, bcd_digit_1_b, bcd_digit_1_c, bcd_digit_1_d, bcd_digit_1_e, bcd_digit_1_f,
       bcd_digit_1_g, bcd_digit_1_h, bcd_digit_2_a, bcd_digit_2_b, bcd_digit_2_c, bcd_digit_2_d,
       bcd_digit_2_e, bcd_digit_2_f, bcd_digit_2_g, bcd_digit_2_h;

  BCD_Digit bcd_digit_1 (
    .IN(in_1[7:4]), .A(bcd_digit_1_a), .B(bcd_digit_1_b), .C(bcd_digit_1_c), .D(bcd_digit_1_d),
    .E(bcd_digit_1_e), .F(bcd_digit_1_f), .G(bcd_digit_1_g), .H(bcd_digit_1_h));
  _7_Segment_Display u_7_segment_display_1 (
    .g(bcd_digit_1_a), .f(bcd_digit_1_b), .a(bcd_digit_1_c), .b(bcd_digit_1_d), .e(bcd_digit_1_e),
    .d(bcd_digit_1_f), .c(bcd_digit_1_g), .dp(bcd_digit_1_h));
  BCD_Digit bcd_digit_2 (
    .IN(in_1[3:0]), .A(bcd_digit_2_a), .B(bcd_digit_2_b), .C(bcd_digit_2_c), .D(bcd_digit_2_d),
    .E(bcd_digit_2_e), .F(bcd_digit_2_f), .G(bcd_digit_2_g), .H(bcd_digit_2_h));
  _7_Segment_Display u_7_segment_display_2 (
    .g(bcd_digit_2_a), .f(bcd_digit_2_b), .a(bcd_digit_2_c), .b(bcd_digit_2_d), .e(bcd_digit_2_e),
    .d(bcd_digit_2_f), .c(bcd_digit_2_g), .dp(bcd_digit_2_h));
endmodule

module BCD_Digit (
  input  [3:0] IN,
  output A,
  output B,
  output C,
  output D,
  output E,
  output F,
  output G,
  output H
);

  wire and_1_out, and_2_out, and_3_out, and_4_out, and_5_out, and_6_out, and_7_out, and_8_out, and_9_out,
       and_10_out, and_11_out, and_12_out, and_13_out, and_14_out, and_15_out, and_16_out, and_17_out,
       and_18_out, and_19_out, and_20_out, and_21_out, and_22_out, and_23_out, and_24_out, and_25_out,
       and_26_out, not_1_out, not_2_out, not_3_out, not_4_out, not_5_out, not_6_out, not_7_out, not_8_out,
       not_9_out, not_10_out, not_11_out, not_12_out, not_13_out, not_14_out, not_15_out, not_16_out,
       not_17_out, not_18_out, not_19_out, not_20_out, not_21_out, not_22_out, not_23_out, not_24_out,
       not_25_out, not_26_out, not_27_out, not_28_out, not_29_out, not_30_out;

  not not_1 (not_1_out, IN[1]);
  not not_2 (not_2_out, IN[0]);
  not not_3 (not_3_out, IN[2]);
  not not_4 (not_4_out, IN[1]);
  not not_5 (not_5_out, IN[0]);
  not not_6 (not_6_out, IN[0]);
  not not_7 (not_7_out, IN[1]);
  not not_8 (not_8_out, IN[0]);
  not not_9 (not_9_out, IN[2]);
  not not_10 (not_10_out, IN[3]);
  not not_11 (not_11_out, IN[2]);
  not not_12 (not_12_out, IN[3]);
  not not_13 (not_13_out, IN[0]);
  not not_14 (not_14_out, IN[1]);
  not not_15 (not_15_out, IN[3]);
  not not_16 (not_16_out, IN[3]);
  not not_17 (not_17_out, IN[1]);
  not not_18 (not_18_out, IN[2]);
  not not_19 (not_19_out, IN[0]);
  not not_20 (not_20_out, IN[0]);
  not not_21 (not_21_out, IN[2]);
  not not_22 (not_22_out, IN[0]);
  not not_23 (not_23_out, IN[2]);
  not not_24 (not_24_out, IN[1]);
  not not_25 (not_25_out, IN[0]);
  not not_26 (not_26_out, IN[2]);
  not not_27 (not_27_out, IN[3]);
  not not_28 (not_28_out, IN[3]);
  not not_29 (not_29_out, IN[1]);
  not not_30 (not_30_out, IN[2]);
  and and_1 (and_1_out, not_1_out, IN[2]);
  and and_2 (and_2_out, not_2_out, IN[1]);
  and and_3 (and_3_out, IN[1], not_3_out);
  and and_4 (and_4_out, not_4_out, IN[2]);
  and and_5 (and_5_out, not_5_out, IN[1], IN[2]);
  and and_6 (and_6_out, not_6_out, not_7_out);
  and and_7 (and_7_out, IN[0], IN[2]);
  and and_8 (and_8_out, not_8_out, not_9_out);
  and and_9 (and_9_out, IN[1], not_10_out);
  and and_10 (and_10_out, not_11_out, not_12_out);
  and and_11 (and_11_out, not_13_out, not_14_out, not_15_out);
  and and_12 (and_12_out, IN[0], IN[1], not_16_out);
  and and_13 (and_13_out, not_17_out, not_18_out);
  and and_14 (and_14_out, IN[2], IN[3]);
  and and_15 (and_15_out, not_19_out, IN[1]);
  and and_16 (and_16_out, IN[1], IN[3]);
  and and_17 (and_17_out, not_20_out, not_21_out);
  and and_18 (and_18_out, not_22_out, IN[1]);
  and and_19 (and_19_out, IN[1], not_23_out);
  and and_20 (and_20_out, IN[0], not_24_out, IN[2]);
  and and_21 (and_21_out, not_25_out, not_26_out);
  and and_22 (and_22_out, IN[2], not_27_out);
  and and_23 (and_23_out, IN[0], not_28_out);
  and and_24 (and_24_out, not_29_out, not_30_out);
  and and_25 (and_25_out, IN[1], IN[3]);
  and and_26 (and_26_out, IN[2], IN[3]);
  or or_1 (A, and_1_out, IN[3], and_2_out, and_3_out);
  or or_2 (B, and_4_out, IN[3], and_5_out, and_6_out);
  or or_3 (C, and_7_out, IN[3], and_8_out, and_9_out);
  or or_4 (D, and_10_out, and_11_out, and_12_out, and_13_out);
  or or_5 (E, and_14_out, and_15_out, and_16_out, and_17_out);
  or or_6 (F, IN[3], and_18_out, and_19_out, and_20_out, and_21_out);
  or or_7 (G, and_22_out, and_23_out, and_24_out);
  or or_8 (H, and_25_out, and_26_out);
endmodule
