// Logisim project lab08.circ as structural Verilog: 3 circuits, main circuit main
module main (
  input  [7:0] in_1,
  input  [7:0] in_2,
  input  [3:0] in_3,
  output [7:0] out_4,
  output out_5,
  output out_6
);

  _8BitAlu u_8bitalu_1 (.A(in_1), .B(in_2), .Operation(in_3), .Result(out_4), .Zero(out_5), .Overflow(out_6));
endmodule

module _1BitAlu (
  input  Ainvert,
  input  Binvert,
  input  CarryIn,
  input  [1:0] Operation,
  input  A,
  input  B,
  input  Less,
  output Result,
  output CarryOut,
  output Set
);

  wire and_1_out, multiplexer_1_out, multiplexer_2_out, not_1_out, not_2_out, or_1_out;

  Multiplexer #(.enable("false")) multiplexer_1 (.in0(A), .in1(not_1_out), .out(multiplexer_1_out), .sel(Ainvert));
  not not_1 (not_1_out, A);
  Multiplexer #(.enable("false")) multiplexer_2 (.in0(B), .in1(not_2_out), .out(multiplexer_2_out), .sel(Binvert));
  not not_2 (not_2_out, B);
  and and_1 (and_1_out, multiplexer_1_out, multiplexer_2_out);
  or or_1 (or_1_out, multiplexer_1_out, multiplexer_2_out);
  Adder #(.width(1)) adder_1 (.a(multiplexer_1_out), .b(multiplexer_2_out), .out(Set), .cin(CarryIn), .cout(CarryOut));
  Multiplexer #(.select(2), .enable("false")) multiplexer_3 (
    .in0(and_1_out), .in1(or_1_out), .in2(Set), .in3(Less), .out(Result), .sel(Operation));
endmodule

module _8BitAlu (
  input  [3:0] Operation,
  input  [7:0] A,
  input  [7:0] B,
  output [7:0] Result,
  output Zero,
  output Overflow
);

  wire n1bitalu_1_carryout, n1bitalu_1_set, n1bitalu_2_carryout, n1bitalu_2_set, n1bitalu_3_carryout,
       n1bitalu_3_set, n1bitalu_4_carryout, n1bitalu_4_set, n1bitalu_5_carryout, n1bitalu_5_set,
       n1bitalu_6_carryout, n1bitalu_6_set, n1bitalu_7_carryout, n1bitalu_7_set, n1bitalu_8_set, or_1_out,
       xor_1_out;

  xor xor_1 (xor_1_out, n1bitalu_8_set, Overflow);
  _1BitAlu u_1bitalu_1 (
    .A(B[0]), .B(A[0]), .Less(xor_1_out), .Ainvert(Operation[3]), .Binvert(Operation[2]),
    .CarryIn(Operation[2]), .Operation(Operation[1:0]), .CarryOut(n1bitalu_1_carryout), .Set(n1bitalu_1_set),
    .Result(Result[0]));
  _1BitAlu u_1bitalu_2 (
    .A(B[1]), .B(A[1]), .Less(1'b0), .Ainvert(Operation[3]), .Binvert(Operation[2]),
    .CarryIn(n1bitalu_1_carryout), .Operation(Operation[1:0]), .CarryOut(n1bitalu_2_carryout),
    .Set(n1bitalu_2_set), .Result(Result[1]));
  _1BitAlu u_1bitalu_3 (
    .A(B[2]), .B(A[2]), .Less(1'b0), .Ainvert(Operation[3]), .Binvert(Operation[2]),
    .CarryIn(n1bitalu_2_carryout), .Operation(Operation[1:0]), .CarryOut(n1bitalu_3_carryout),
    .Set(n1bitalu_3_set), .Result(Result[2]));
  _1BitAlu u_1bitalu_4 (
    .A(B[3]), .B(A[3]), .Less(1'b0), .Ainvert(Operation[3]), .Binvert(Operation[2]),
    .CarryIn(n1bitalu_3_carryout), .Operation(Operation[1:0]), .CarryOut(n1bitalu_4_carryout),
    .Set(n1bitalu_4_set), .Result(Result[3]));
  _1BitAlu u_1bitalu_5 (
    .A(B[4]), .B(A[4]), .Less(1'b0), .Ainvert(Operation[3]), .Binvert(Operation[2]),
    .CarryIn(n1bitalu_4_carryout), .Operation(Operation[1:0]), .CarryOut(n1bitalu_5_carryout),
    .Set(n1bitalu_5_set), .Result(Result[4]));
  _1BitAlu u_1bitalu_6 (
    .A(B[5]), .B(A[5]), .Less(1'b0), .Ainvert(Operation[3]), .Binvert(Operation[2]),
    .CarryIn(n1bitalu_5_carryout), .Operation(Operation[1:0]), .CarryOut(n1bitalu_6_carryout),
    .Set(n1bitalu_6_set), .Result(Result[5]));
  _1BitAlu u_1bitalu_7 (
    .A(B[6]), .B(A[6]), .Less(1'b0), .Ainvert(Operation[3]), .Binvert(Operation[2]),
    .CarryIn(n1bitalu_6_carryout), .Operation(Operation[1:0]), .CarryOut(n1bitalu_7_carryout),
    .Set(n1bitalu_7_set), .Result(Result[6]));
  _1BitAlu u_1bitalu_8 (
    .A(B[7]), .B(A[7]), .Less(1'b0), .Ainvert(Operation[3]), .Binvert(Operation[2]),
    .CarryIn(n1bitalu_7_carryout), .Operation(Operation[1:0]), .CarryOut(Overflow), .Set(n1bitalu_8_set),
    .Result(Result[7]));
  not not_1 (Zero, or_1_out);
  or or_1 (or_1_out, Result[0], Result[1], Result[2], Result[3], Result[4], Result[5], Result[6], Result[7]);
endmodule
